// Logisim project ALU.circ as structural Verilog: 1 circuit, main circuit main
module main (
  input  A3,
  input  A2,
  input  A1,
  input  in_4,
  input  B3,
  input  B2,
  input  B1,
  input  B0,
  input  S1,
  input  S0
);

  wire A__B, A__B_t, A_B, and_1_out, and_5_out, and_6_out, and_7_out, and_8_out, and_9_out, and_10_out,
       and_11_out, and_12_out, and_13_out, and_14_out, and_15_out, and_16_out, and_17_out, and_18_out,
       and_19_out, and_20_out, and_21_out, and_22_out, and_23_out, and_24_out, and_25_out, and_26_out,
       and_27_out, and_28_out, and_29_out, and_30_out, and_31_out, and_32_out, and_33_out, and_34_out,
       and_35_out, and_36_out, and_37_out, and_38_out, and_39_out, and_40_out, and_41_out, and_42_out,
       and_43_out, and_44_out, and_45_out, and_46_out, and_47_out, and_48_out, and_49_out, not_1_out,
       not_2_out, not_3_out, not_4_out, not_5_out, not_6_out, not_7_out, not_8_out, not_9_out, not_10_out,
       not_11_out, not_12_out, or_1_out, or_2_out, or_3_out, or_4_out, or_5_out, or_6_out, or_7_out,
       or_8_out, or_9_out, or_10_out, or_11_out, or_12_out, or_13_out, or_14_out, or_15_out, or_16_out,
       or_17_out, or_18_out, or_19_out, or_20_out, or_21_out, or_22_out, or_23_out, or_24_out, or_25_out,
       or_26_out, or_27_out, or_28_out, or_29_out, or_30_out, or_31_out, or_32_out, xor_1_out, xor_2_out,
       xor_3_out, xor_4_out, xor_5_out, xor_6_out, xor_7_out, xor_8_out, xor_9_out, xor_10_out, xor_11_out,
       xor_12_out, xor_13_out, xor_14_out, xor_15_out, xor_16_out, xor_17_out, xor_18_out, xor_19_out,
       xor_20_out, xor_21_out, xor_22_out, xor_23_out, xor_24_out;

  not not_1 (not_1_out, S1);
  not not_2 (not_2_out, S0);
  not not_3 (not_3_out, S1);
  not not_4 (not_4_out, S0);
  and and_1 (and_1_out, not_1_out, not_2_out);
  and and_2 (A_B, not_3_out, S0);
  and and_3 (A__B, S1, not_4_out);
  and and_4 (A__B_t, S1, S0);
  and and_5 (and_5_out, A3, B3);
  or or_1 (or_1_out, A3, B3);
  and and_6 (and_6_out, or_1_out, or_4_out);
  or or_2 (or_2_out, and_5_out, and_6_out);
  xor xor_1 (xor_1_out, B3, or_4_out);
  xor xor_2 (xor_2_out, A3, xor_1_out);
  and and_7 (and_7_out, A2, B2);
  or or_3 (or_3_out, A2, B2);
  and and_8 (and_8_out, or_3_out, or_6_out);
  or or_4 (or_4_out, and_7_out, and_8_out);
  xor xor_3 (xor_3_out, A2, xor_4_out);
  and and_9 (and_9_out, and_1_out, xor_2_out);
  xor xor_4 (xor_4_out, B2, or_6_out);
  and and_10 (and_10_out, and_1_out, xor_3_out);
  and and_11 (and_11_out, A1, B1);
  and and_12 (and_12_out, and_1_out, xor_5_out);
  or or_5 (or_5_out, A1, B1);
  and and_13 (and_13_out, or_5_out, or_8_out);
  or or_6 (or_6_out, and_11_out, and_13_out);
  and and_14 (and_14_out, and_1_out, xor_8_out);
  LED led_1 (.in(or_2_out));
  xor xor_5 (xor_5_out, A1, xor_6_out);
  xor xor_6 (xor_6_out, B1, or_8_out);
  LED led_2 (.in(or_14_out));
  and and_15 (and_15_out, in_4, B0);
  or or_7 (or_7_out, in_4, B0);
  and and_16 (and_16_out, or_7_out, 1'b0);
  or or_8 (or_8_out, and_15_out, and_16_out);
  LED led_3 (.in(or_9_out));
  not not_5 (not_5_out, or_15_out);
  not not_6 (not_6_out, or_9_out);
  not not_7 (not_7_out, or_10_out);
  and and_17 (and_17_out, not_6_out, not_7_out, not_5_out, not_8_out);
  LED led_4 (.in(and_17_out));
  xor xor_7 (xor_7_out, B0, 1'b0);
  xor xor_8 (xor_8_out, in_4, xor_7_out);
  not not_8 (not_8_out, or_16_out);
  or or_9 (or_9_out, and_9_out, and_26_out, and_39_out, and_46_out);
  LED led_5 (.in(or_9_out));
  and and_18 (and_18_out, 1'b0, not_9_out);
  and and_19 (and_19_out, A3, xor_9_out);
  or or_10 (or_10_out, and_10_out, and_27_out, and_41_out, and_47_out);
  LED led_6 (.in(or_10_out));
  or or_11 (or_11_out, 1'b0, not_9_out);
  and and_20 (and_20_out, or_11_out, or_20_out);
  or or_12 (or_12_out, and_18_out, and_20_out);
  LED led_7 (.in(or_12_out));
  or or_13 (or_13_out, A3, xor_9_out);
  and and_21 (and_21_out, or_13_out, or_18_out);
  or or_14 (or_14_out, and_19_out, and_21_out);
  or or_15 (or_15_out, and_12_out, and_28_out, and_43_out, and_48_out);
  LED led_8 (.in(or_15_out));
  or or_16 (or_16_out, and_14_out, and_30_out, and_45_out, and_49_out);
  LED led_9 (.in(or_16_out));
  not not_9 (not_9_out, B3);
  xor xor_9 (xor_9_out, 1'b0, xor_12_out);
  xor xor_10 (xor_10_out, xor_9_out, or_18_out);
  xor xor_11 (xor_11_out, A3, xor_10_out);
  xor xor_12 (xor_12_out, not_9_out, or_20_out);
  and and_22 (and_22_out, A2, xor_15_out);
  and and_23 (and_23_out, 1'b0, not_10_out);
  or or_17 (or_17_out, A2, xor_15_out);
  and and_24 (and_24_out, or_17_out, or_22_out);
  or or_18 (or_18_out, and_22_out, and_24_out);
  or or_19 (or_19_out, 1'b0, not_10_out);
  and and_25 (and_25_out, or_19_out, or_24_out);
  or or_20 (or_20_out, and_23_out, and_25_out);
  and and_26 (and_26_out, A_B, xor_11_out);
  xor xor_13 (xor_13_out, A2, xor_16_out);
  and and_27 (and_27_out, A_B, xor_13_out);
  not not_10 (not_10_out, B2);
  xor xor_14 (xor_14_out, not_10_out, or_24_out);
  xor xor_15 (xor_15_out, 1'b0, xor_14_out);
  xor xor_16 (xor_16_out, xor_15_out, or_22_out);
  and and_28 (and_28_out, A_B, xor_20_out);
  and and_29 (and_29_out, A1, xor_18_out);
  and and_30 (and_30_out, A_B, xor_22_out);
  and and_31 (and_31_out, 1'b0, not_11_out);
  or or_21 (or_21_out, A1, xor_18_out);
  or or_22 (or_22_out, and_29_out, and_33_out);
  or or_23 (or_23_out, 1'b0, not_11_out);
  and and_32 (and_32_out, or_23_out, or_26_out);
  or or_24 (or_24_out, and_31_out, and_32_out);
  and and_33 (and_33_out, or_21_out, or_28_out);
  not not_11 (not_11_out, B1);
  xor xor_17 (xor_17_out, not_11_out, or_26_out);
  xor xor_18 (xor_18_out, 1'b0, xor_17_out);
  xor xor_19 (xor_19_out, xor_18_out, or_28_out);
  xor xor_20 (xor_20_out, A1, xor_19_out);
  and and_34 (and_34_out, 1'b1, not_12_out);
  and and_35 (and_35_out, in_4, xor_24_out);
  or or_25 (or_25_out, 1'b1, not_12_out);
  or or_26 (or_26_out, and_34_out, and_37_out);
  or or_27 (or_27_out, in_4, xor_24_out);
  and and_36 (and_36_out, or_27_out, 1'b0);
  or or_28 (or_28_out, and_35_out, and_36_out);
  and and_37 (and_37_out, or_25_out, 1'b0);
  not not_12 (not_12_out, B0);
  xor xor_21 (xor_21_out, xor_24_out, 1'b0);
  xor xor_22 (xor_22_out, in_4, xor_21_out);
  xor xor_23 (xor_23_out, not_12_out, 1'b0);
  xor xor_24 (xor_24_out, 1'b1, xor_23_out);
  and and_38 (and_38_out, A3, B3);
  and and_39 (and_39_out, A__B, and_38_out);
  and and_40 (and_40_out, A2, B2);
  and and_41 (and_41_out, A__B, and_40_out);
  and and_42 (and_42_out, A1, B1);
  and and_43 (and_43_out, A__B, and_42_out);
  and and_44 (and_44_out, in_4, B0);
  and and_45 (and_45_out, A__B, and_44_out);
  or or_29 (or_29_out, A3, B3);
  and and_46 (and_46_out, A__B_t, or_29_out);
  or or_30 (or_30_out, A2, B2);
  and and_47 (and_47_out, A__B_t, or_30_out);
  or or_31 (or_31_out, A1, B1);
  and and_48 (and_48_out, A__B_t, or_31_out);
  or or_32 (or_32_out, in_4, B0);
  and and_49 (and_49_out, A__B_t, or_32_out);

  // Notes on the sheet:
  //   SELECTOR
  //   A+B
  //   A-B
  //   A&B
  //   A|B
  //   A0
  //   C
  //   S0
  //   SUMADOR
  //   C
  //   Vladimir Suarez Vega
  //   S0
  //   ISC 3° "B"
  //   C
  //   SUMA CARRY
  //   (SUMA INCORRECTA)
  //   PROFESOR: Luis Alejandro Florez Oropeza
  //   S0
  //   RESTA CARRY
  //   (OVERFLOW)
  //   C
  //   NUMEROS
  //   NEGATIVOS
  //   BANDERAS (FLAGS)
  //   CERO
  //   S0
  //   Ci
  //   C
  //   SALIDAS (LEDS)
  //   C
  //   S0
  //   S0
  //   C
  //   C
  //   S0
  //   S0
  //   RESTADOR
  //   COMPLEMENTO A 2
  //   C
  //   C
  //   S0
  //   S0
  //   C
  //   C
  //   S0
  //   Ci
  //   Ci
  //   AND
  //   OR
endmodule
