// Logisim project Maquina HOLA.circ as structural Verilog: 1 circuit, main circuit main
module main (
  input  in_1
);

  wire A, AN, and_1_out, and_2_out, and_3_out, and_4_out, B, BN, clock_1_out, not_1_out, or_1_out, or_2_out,
       or_3_out, xor_1_out;

  not not_1 (not_1_out, in_1);
  and and_1 (and_1_out, A, not_1_out);
  and and_2 (and_2_out, in_1, B);
  and and_3 (and_3_out, B, not_1_out);
  and and_4 (and_4_out, AN, in_1);
  or or_1 (or_1_out, and_1_out, and_2_out);
  or or_2 (or_2_out, and_3_out, and_4_out);
  Clock clock_1 (.out(clock_1_out));
  D_Flip_Flop d_ff_1 (.clk(clock_1_out), .D(or_1_out), .Q(A), .Qn(AN));  // open: preset, en, reset
  D_Flip_Flop d_ff_2 (.clk(clock_1_out), .D(or_2_out), .Q(B), .Qn(BN));  // open: preset, en, reset
  xor xor_1 (xor_1_out, A, B);
  _7_Segment_Display u_7_segment_display_1 (
    .g(BN), .f(1'b1), .a(xor_1_out), .b(or_3_out), .e(1'b1), .d(B), .c(or_3_out));  // open: dp
  or or_3 (or_3_out, AN, BN);

  // Notes on the sheet:
  //   Alumno: Vladimir Suárez Vega       ID: 548562
  //   ISC 3° "B"
endmodule
