// Logisim project Maquina cuenta de 0 a 4.circ as structural Verilog: 1 circuit, main circuit main
module main (
  input  in_1
);

  wire A, AN, and_1_out, and_2_out, and_3_out, and_4_out, and_5_out, and_6_out, and_7_out, B, BN, C,
       clock_1_out, CN, not_1_out, or_1_out, or_2_out, or_3_out;

  not not_1 (not_1_out, in_1);
  and and_1 (and_1_out, not_1_out, A);
  and and_2 (and_2_out, in_1, B, C);
  and and_3 (and_3_out, B, CN);
  and and_4 (and_4_out, not_1_out, B);
  and and_5 (and_5_out, in_1, C, BN);
  and and_6 (and_6_out, in_1, AN, CN);
  and and_7 (and_7_out, C, not_1_out);
  or or_1 (or_1_out, and_1_out, and_2_out);
  D_Flip_Flop A_star (.clk(clock_1_out), .D(or_1_out), .Q(A), .Qn(AN));  // open: preset, en, reset
  D_Flip_Flop B_star (.clk(clock_1_out), .D(or_2_out), .Q(B), .Qn(BN));  // open: preset, en, reset
  or or_2 (or_2_out, and_3_out, and_4_out, and_5_out);
  or or_3 (or_3_out, and_6_out, and_7_out);
  D_Flip_Flop C_star (.clk(clock_1_out), .D(or_3_out), .Q(C), .Qn(CN));  // open: preset, en, reset
  Clock clock_1 (.out(clock_1_out));
  LED u_A (.in(A));
  LED u_B (.in(B));
  LED u_C (.in(C));

  // Notes on the sheet:
  //   ALUMNO: Vladimir Suárez Vega               ID:548562
  //   ISC 3° "B"
endmodule
