// Logisim project Maquina de 3 unos.circ as structural Verilog: 1 circuit, main circuit main
module main (
  input  in_1
);

  wire and_1_out, and_2_out, and_3_out, d_ff_1_q, d_ff_1_qn, d_ff_2_q, undriven;

  and and_1 (and_1_out, in_1, d_ff_2_q, d_ff_1_qn);
  and and_2 (and_2_out, d_ff_1_qn, in_1);
  Clock clock_1 ();  // open: out
  D_Flip_Flop d_ff_1 (.clk(undriven), .D(and_1_out), .Q(d_ff_1_q), .Qn(d_ff_1_qn));  // open: preset, en, reset
  D_Flip_Flop d_ff_2 (.clk(undriven), .D(and_2_out), .Q(d_ff_2_q));  // open: Qn, preset, en, reset
  and and_3 (and_3_out, in_1, d_ff_1_q);
  LED led_1 (.in(and_3_out));
endmodule
