// Logisim project Restador.circ as structural Verilog: 1 circuit, main circuit main
module main (
  input  A3,
  input  A2,
  input  A1,
  input  in_4,
  input  B3,
  input  B2,
  input  B1,
  input  B0
);

  wire and_1_out, and_2_out, and_3_out, and_4_out, and_5_out, and_6_out, and_7_out, and_8_out, and_9_out,
       and_10_out, and_11_out, and_12_out, and_13_out, and_14_out, and_15_out, and_16_out, and_17_out,
       and_18_out, and_19_out, and_20_out, and_21_out, and_22_out, and_23_out, and_24_out, not_1_out,
       not_2_out, not_3_out, not_4_out, or_1_out, or_2_out, or_3_out, or_4_out, or_5_out, or_6_out, or_7_out,
       or_8_out, or_9_out, or_10_out, or_11_out, or_12_out, or_13_out, or_14_out, or_15_out, or_16_out,
       or_17_out, or_18_out, or_19_out, or_20_out, or_21_out, or_22_out, or_23_out, or_24_out, xor_1_out,
       xor_2_out, xor_3_out, xor_4_out, xor_5_out, xor_6_out, xor_7_out, xor_8_out, xor_9_out, xor_10_out,
       xor_11_out, xor_12_out, xor_13_out, xor_14_out, xor_15_out, xor_16_out, xor_17_out, xor_18_out,
       xor_19_out, xor_20_out, xor_21_out, xor_22_out, xor_23_out, xor_24_out;

  and and_1 (and_1_out, A3, B3);
  or or_1 (or_1_out, A3, B3);
  or or_2 (or_2_out, and_1_out, and_2_out);
  LED led_1 (.in(or_2_out));
  and and_2 (and_2_out, or_1_out, or_4_out);
  xor xor_1 (xor_1_out, B3, or_4_out);
  xor xor_2 (xor_2_out, A3, xor_1_out);
  LED led_2 (.in(xor_2_out));
  and and_3 (and_3_out, A2, B2);
  or or_3 (or_3_out, A2, B2);
  and and_4 (and_4_out, or_3_out, or_6_out);
  or or_4 (or_4_out, and_3_out, and_4_out);
  xor xor_3 (xor_3_out, B2, or_6_out);
  xor xor_4 (xor_4_out, A2, xor_3_out);
  LED led_3 (.in(xor_4_out));
  and and_5 (and_5_out, A1, B1);
  or or_5 (or_5_out, A1, B1);
  and and_6 (and_6_out, or_5_out, or_8_out);
  or or_6 (or_6_out, and_5_out, and_6_out);
  xor xor_5 (xor_5_out, B1, or_8_out);
  xor xor_6 (xor_6_out, A1, xor_5_out);
  LED led_4 (.in(xor_6_out));
  and and_7 (and_7_out, in_4, B0);
  or or_7 (or_7_out, in_4, B0);
  and and_8 (and_8_out, or_7_out, 1'b0);
  or or_8 (or_8_out, and_7_out, and_8_out);
  xor xor_7 (xor_7_out, B0, 1'b0);
  xor xor_8 (xor_8_out, in_4, xor_7_out);
  LED led_5 (.in(xor_8_out));
  and and_9 (and_9_out, A3, xor_10_out);
  and and_10 (and_10_out, 1'b0, not_1_out);
  or or_9 (or_9_out, and_9_out, and_12_out);
  LED led_6 (.in(or_9_out));
  or or_10 (or_10_out, 1'b0, not_1_out);
  and and_11 (and_11_out, or_10_out, or_14_out);
  or or_11 (or_11_out, and_10_out, and_11_out);
  LED led_7 (.in(or_11_out));
  or or_12 (or_12_out, A3, xor_10_out);
  and and_12 (and_12_out, or_12_out, or_16_out);
  not not_1 (not_1_out, B3);
  xor xor_9 (xor_9_out, not_1_out, or_14_out);
  xor xor_10 (xor_10_out, 1'b0, xor_9_out);
  xor xor_11 (xor_11_out, xor_10_out, or_16_out);
  xor xor_12 (xor_12_out, A3, xor_11_out);
  LED led_8 (.in(xor_12_out));
  and and_13 (and_13_out, 1'b0, not_2_out);
  and and_14 (and_14_out, A2, xor_16_out);
  or or_13 (or_13_out, 1'b0, not_2_out);
  or or_14 (or_14_out, and_13_out, and_16_out);
  or or_15 (or_15_out, A2, xor_16_out);
  and and_15 (and_15_out, or_15_out, or_19_out);
  or or_16 (or_16_out, and_14_out, and_15_out);
  and and_16 (and_16_out, or_13_out, or_17_out);
  not not_2 (not_2_out, B2);
  xor xor_13 (xor_13_out, xor_16_out, or_19_out);
  xor xor_14 (xor_14_out, A2, xor_13_out);
  LED led_9 (.in(xor_14_out));
  xor xor_15 (xor_15_out, not_2_out, or_17_out);
  xor xor_16 (xor_16_out, 1'b0, xor_15_out);
  and and_17 (and_17_out, 1'b0, not_3_out);
  and and_18 (and_18_out, A1, xor_19_out);
  or or_17 (or_17_out, and_17_out, and_20_out);
  or or_18 (or_18_out, A1, xor_19_out);
  and and_19 (and_19_out, or_18_out, or_24_out);
  or or_19 (or_19_out, and_18_out, and_19_out);
  or or_20 (or_20_out, 1'b0, not_3_out);
  and and_20 (and_20_out, or_20_out, or_22_out);
  xor xor_17 (xor_17_out, A1, xor_20_out);
  LED led_10 (.in(xor_17_out));
  not not_3 (not_3_out, B1);
  xor xor_18 (xor_18_out, not_3_out, or_22_out);
  xor xor_19 (xor_19_out, 1'b0, xor_18_out);
  xor xor_20 (xor_20_out, xor_19_out, or_24_out);
  and and_21 (and_21_out, 1'b1, not_4_out);
  and and_22 (and_22_out, in_4, xor_21_out);
  or or_21 (or_21_out, 1'b1, not_4_out);
  and and_23 (and_23_out, or_21_out, 1'b0);
  or or_22 (or_22_out, and_21_out, and_23_out);
  or or_23 (or_23_out, in_4, xor_21_out);
  and and_24 (and_24_out, or_23_out, 1'b0);
  or or_24 (or_24_out, and_22_out, and_24_out);
  not not_4 (not_4_out, B0);
  xor xor_21 (xor_21_out, 1'b1, xor_24_out);
  xor xor_22 (xor_22_out, xor_21_out, 1'b0);
  xor xor_23 (xor_23_out, in_4, xor_22_out);
  LED led_11 (.in(xor_23_out));
  xor xor_24 (xor_24_out, not_4_out, 1'b0);

  // Notes on the sheet:
  //   A0
  //   C
  //   S0
  //   C
  //   SUMADOR
  //   Vladimir Suarez Vega
  //   S0
  //   C
  //   S0
  //   C
  //   Ci
  //   S0
  //   C
  //   C
  //   S0
  //   S0
  //   C
  //   C
  //   S0
  //   S0
  //   RESTADOR
  //   COMPLEMENTO A 2
  //   C
  //   C
  //   S0
  //   S0
  //   C
  //   C
  //   Ci
  //   S0
  //   Ci
endmodule
